# Fritzing sketch keypad (saved by Fritzing 0.9.2b)
breadboards: 1

parts:
  J1 = Piezo Speaker
  Part1 = Arduino Uno (Rev3) - ICSP
  KEYPAD1 = Membrane Matrix Keypad
  LED1 = RGB LED (com. cathode, rbg) [package="5 mm [THT]"]
  Q1 = Basic FET N-Channel [package="TO220 [THT]"]
  R1 = Resistor [tolerance=±5% resistance=220 package="2010 [SMD]"]
  R2 = Resistor [tolerance=±5% resistance=220 package="2010 [SMD]"]
  R3 = Resistor [tolerance=±5% resistance=220 package="2010 [SMD]"]
  R4 = Resistor [tolerance=±5% resistance=220 package="2010 [SMD]"]
  BAT1 = BC9VPC [package=bc9vpc]
  L1 = Solenoid

nets:
  N1: J1.pin1, Part1.GND, LED1.common_cathode, Q1.source, BAT1.V-
  N2: J1.pin2, Part1.D13/SCK
  N3: Part1.ICSP_MOSI, Part1.D11_PWM/MOSI, R2.Pin_1
  N4: Part1.D9_PWM, R1.Pin_1
  N5: Part1.D10_PWM/SS, R3.Pin_1
  N6: Part1.D12/MISO, R4.Pin_1
  N7: Part1.D1/TX, KEYPAD1.7
  N8: Part1.D2, KEYPAD1.6
  N9: Part1.D3_PWM, KEYPAD1.5
  N10: Part1.D4, KEYPAD1.4
  N11: Part1.D5_PWM, KEYPAD1.3
  N12: Part1.D6_PWM, KEYPAD1.2
  N13: Part1.D7, KEYPAD1.1
  N14: LED1.red_anode, R2.Pin_0
  N15: LED1.blue_anode, R3.Pin_0
  N16: LED1.green_anode, R1.Pin_0
  N17: Q1.gate, R4.Pin_0
  N18: Q1.drain, L1.pin1
  N19: BAT1.V+, L1.pin2

notes:
  12V Door Latch
  12V 0.5 A Power Supply

custom parts:
  Membrane Matrix Keypad: Membrane Matrix 3x4 Keypad
